# Fritzing sketch bluetooth (saved by Fritzing 0.9.6b)
breadboards: 1

parts:
  Part1 = Arduino Nano (Rev3.0) (ICSP)
  R2 = Resistor [tolerance=±5% power=0.25W resistance=10k package=THT]
  Part2 = Bluetooth HM-10
  R1 = Resistor [tolerance=±5% power=0.25W resistance=18k package=THT]

nets:
  N1: Part1.D1/TX, R2.Pin_0
  N2: Part1.D0/RX, Part2.TXD
  GND: Part1.GND, Part2.GND, R1.Pin_0
  5V: Part1.5V, Part2.VCC
  N3: R2.Pin_1, Part2.RXD, R1.Pin_1

notes:
  R1 = 18 kΩ
  R2 = 10 kΩ
  Pink wire = jumper under the Arduino Nano
